// Logisim project scheme.circ as structural Verilog: 7 circuits, main circuit Screen
module main (
);

  wire cdm_8_mark5_1_p2, cdm_8_mark5_1_p8, code, data, mem, rd_wr, tact;
  wire [7:0] cdm_8_mark5_1_p5, cdm_8_mark5_1_p6, cdm_8_mark5_1_p7, controlled_buffer_2_out;

  Clock clock_1 (.out(tact));
  // CdM_8_mark5 cdm_8_mark5_1: pin names not known; wires that end beside it: tact, cdm_8_mark5_1_p2, mem, rd_wr, cdm_8_mark5_1_p5, cdm_8_mark5_1_p6, cdm_8_mark5_1_p7, cdm_8_mark5_1_p8
  assign cdm_8_mark5_1_p7 = rd_wr ? controlled_buffer_2_out : 8'bz;  // Controlled_Buffer controlled_buffer_1
  Demultiplexer #(.enable("false")) demultiplexer_1 (.out0(code), .out1(data), .in(mem), .sel(cdm_8_mark5_1_p2));
  assign controlled_buffer_2_out = cdm_8_mark5_1_p8 ? cdm_8_mark5_1_p6 : 8'bz;  // Controlled_Buffer controlled_buffer_2
  not not_1 (cdm_8_mark5_1_p8, rd_wr);
  ROM rom_1 ();  // open: addr, data, sel
  ROM rom_2 (.addr(cdm_8_mark5_1_p5), .data(controlled_buffer_2_out), .sel(code));
  RAM ram_1 (.addr(cdm_8_mark5_1_p5), .data(controlled_buffer_2_out), .sel(data), .clk(tact), .ld(rd_wr));  // open: clr

  // Notes on the sheet:
  //   instr memory
  //   data memory
endmodule

module Screen (
);

  wire game_state, left, lose, pause, right, start;
  wire [31:0] info_screen_1_out_4, info_screen_1_out_5, info_screen_1_out_6, info_screen_1_out_7,
       info_screen_1_out_8, info_screen_1_out_9, info_screen_1_out_10, screen_options_1_out_7,
       screen_options_1_out_8, screen_options_1_out_9, screen_options_1_out_10, screen_options_1_out_12,
       screen_options_1_out_13, screen_options_1_out_14, screen_options_1_out_15, screen_options_1_out_16,
       screen_options_1_out_17, screen_options_1_out_18, screen_options_1_out_19, screen_options_1_out_20,
       screen_options_1_out_21, screen_options_1_out_22, screen_options_1_out_23, screen_options_1_out_24,
       screen_options_1_out_25, screen_options_1_out_26, screen_options_1_out_27, screen_options_1_out_28,
       screen_options_1_out_29, screen_options_1_out_30, screen_options_1_out_31, screen_options_1_out_32,
       screen_options_1_out_33, screen_options_1_out_34, screen_options_1_out_35, screen_options_1_out_36,
       screen_options_1_out_37, screen_options_1_out_38, screen_options_1_out_39;

  start_stop start_stop_1 (.start_stop(start), .state_of_game(game_state), .lose(lose));
  Button Start_stop_2 (.out(start));
  Button u_Pause (.out(pause));
  Button button_1 (.out(left));
  Button button_2 (.out(right));
  DotMatrix #(.inputtype("row"), .matrixcols(32)) dotmatrix_1 (
    .row0(info_screen_1_out_4), .row1(info_screen_1_out_5), .row2(info_screen_1_out_6),
    .row3(info_screen_1_out_7), .row4(info_screen_1_out_8), .row5(info_screen_1_out_9),
    .row6(info_screen_1_out_10));
  Info_Screen info_screen_1 (
    .Lose_indicator(lose), .Start(start), .Pause(pause), .out_4(info_screen_1_out_4),
    .out_5(info_screen_1_out_5), .out_6(info_screen_1_out_6), .out_7(info_screen_1_out_7),
    .out_8(info_screen_1_out_8), .out_9(info_screen_1_out_9), .out_10(info_screen_1_out_10));
  DotMatrix #(.inputtype("row"), .matrixcols(32), .matrixrows(32)) dotmatrix_2 (
    .row0(screen_options_1_out_39), .row1(screen_options_1_out_35), .row2(screen_options_1_out_31),
    .row3(screen_options_1_out_27), .row4(screen_options_1_out_23), .row5(screen_options_1_out_19),
    .row6(screen_options_1_out_15), .row7(screen_options_1_out_10), .row8(screen_options_1_out_38),
    .row9(screen_options_1_out_34), .row10(screen_options_1_out_30), .row11(screen_options_1_out_26),
    .row12(screen_options_1_out_22), .row13(screen_options_1_out_18), .row14(screen_options_1_out_14),
    .row15(screen_options_1_out_9), .row16(screen_options_1_out_37), .row17(screen_options_1_out_33),
    .row18(screen_options_1_out_29), .row19(screen_options_1_out_25), .row20(screen_options_1_out_21),
    .row21(screen_options_1_out_17), .row22(screen_options_1_out_13), .row23(screen_options_1_out_8),
    .row24(screen_options_1_out_36), .row25(screen_options_1_out_32), .row26(screen_options_1_out_28),
    .row27(screen_options_1_out_24), .row28(screen_options_1_out_20), .row29(screen_options_1_out_16),
    .row30(screen_options_1_out_12), .row31(screen_options_1_out_7));
  // DotMatrix #(.inputtype("select"), .matrixcols(31), .matrixrows(32)) dotmatrix_3: pin names not known
  Screen_options screen_options_1 (
    .out_7(screen_options_1_out_7), .out_12(screen_options_1_out_12), .out_16(screen_options_1_out_16),
    .out_20(screen_options_1_out_20), .out_24(screen_options_1_out_24), .out_28(screen_options_1_out_28),
    .out_32(screen_options_1_out_32), .out_36(screen_options_1_out_36), .out_8(screen_options_1_out_8),
    .out_13(screen_options_1_out_13), .out_17(screen_options_1_out_17), .out_21(screen_options_1_out_21),
    .out_25(screen_options_1_out_25), .out_29(screen_options_1_out_29), .out_33(screen_options_1_out_33),
    .out_37(screen_options_1_out_37), .out_9(screen_options_1_out_9), .out_14(screen_options_1_out_14),
    .out_18(screen_options_1_out_18), .out_22(screen_options_1_out_22), .out_26(screen_options_1_out_26),
    .out_30(screen_options_1_out_30), .out_34(screen_options_1_out_34), .out_38(screen_options_1_out_38),
    .out_10(screen_options_1_out_10), .out_15(screen_options_1_out_15), .out_19(screen_options_1_out_19),
    .out_23(screen_options_1_out_23), .out_27(screen_options_1_out_27), .out_31(screen_options_1_out_31),
    .out_35(screen_options_1_out_35), .out_39(screen_options_1_out_39), .start(game_state), .x_left(left),
    .x_right(right), .Lose(lose), .pause(pause));  // open: out_5, out_6
  DotMatrix #(.inputtype("row"), .matrixcols(30), .matrixrows(32), .dotshape("circle")) dotmatrix_4 (.row26(30'h55fff34));  // open: row0, row1, row2, row3, row4, row5, row6, row7, row8, row9, row10, row11, row12, row13, row14, row15, row16, row17, row18, row19, row20, row21, row22, row23, row24, row25, row27, row28, row29, row30, row31
endmodule

module start_stop (
  input  start_stop,
  input  lose,
  output state_of_game
);

  wire not_1_out;

  not not_1 (not_1_out, state_of_game);
  Register #(.width(1)) register_1 (.D(not_1_out), .Q(state_of_game), .clk(start_stop), .clr(lose));  // open: en
endmodule

module Screen_options (
  input  pause,
  input  start,
  input  x_left,
  input  x_right,
  output [30:0] out_5,
  output [31:0] out_6,
  output [31:0] out_7,
  output [31:0] out_8,
  output [31:0] out_9,
  output [31:0] out_10,
  output Lose,
  output [31:0] out_12,
  output [31:0] out_13,
  output [31:0] out_14,
  output [31:0] out_15,
  output [31:0] out_16,
  output [31:0] out_17,
  output [31:0] out_18,
  output [31:0] out_19,
  output [31:0] out_20,
  output [31:0] out_21,
  output [31:0] out_22,
  output [31:0] out_23,
  output [31:0] out_24,
  output [31:0] out_25,
  output [31:0] out_26,
  output [31:0] out_27,
  output [31:0] out_28,
  output [31:0] out_29,
  output [31:0] out_30,
  output [31:0] out_31,
  output [31:0] out_32,
  output [31:0] out_33,
  output [31:0] out_34,
  output [31:0] out_35,
  output [31:0] out_36,
  output [31:0] out_37,
  output [31:0] out_38,
  output [31:0] out_39
);

  wire and_1_out, and_2_out, check_helper_1_out_3, check_helper_2_out_3, check_helper_3_out_3,
       check_helper_4_out_3, check_helper_5_out_3, check_helper_6_out_3, check_helper_7_out_3,
       check_helper_8_out_3, check_helper_9_out_3, check_helper_10_out_3, check_helper_11_out_3,
       check_helper_12_out_3, check_helper_13_out_3, check_helper_14_out_3, check_helper_15_out_3,
       check_helper_16_out_3, check_helper_17_out_3, check_helper_18_out_3, check_helper_19_out_3,
       check_helper_20_out_3, check_helper_21_out_3, check_helper_22_out_3, check_helper_23_out_3,
       check_helper_24_out_3, check_helper_25_out_3, check_helper_26_out_3, check_helper_27_out_3,
       check_helper_28_out_3, check_helper_29_out_3, check_helper_30_out_3, check_helper_31_out_3,
       check_helper_32_out_3, check_helper_33_out_3, check_helper_34_out_3, check_helper_35_out_3,
       check_helper_36_out_3, check_helper_37_out_3, check_helper_38_out_3, check_helper_39_out_3,
       check_helper_40_out_3, check_helper_41_out_3, check_helper_42_out_3, check_helper_43_out_3,
       check_helper_44_out_3, check_helper_45_out_3, check_helper_46_out_3, check_helper_47_out_3,
       check_helper_48_out_3, check_helper_49_out_3, check_helper_50_out_3, check_helper_51_out_3,
       check_helper_52_out_3, check_helper_53_out_3, check_helper_54_out_3, check_helper_55_out_3,
       check_helper_56_out_3, check_helper_57_out_3, check_helper_58_out_3, check_helper_59_out_3,
       check_helper_60_out_3, check_helper_61_out_3, check_helper_62_out_3, check_helper_63_out_3,
       check_helper_64_out_3, clock_1_out, comparator_1_eq, comparator_2_eq, d_ff_1_q, d_ff_2_q, d_ff_3_q,
       d_ff_4_q, d_ff_5_q, down, multiplexer_1_out, multiplexer_44_out, not_1_out, not_2_out, not_4_out,
       not_5_out, not_6_out, not_7_out, not_8_out, not_9_out, not_10_out, not_11_out, not_12_out, not_13_out,
       not_14_out, not_15_out, not_17_out, or_1_out, or_3_out, or_5_out, or_6_out, or_7_out, start_alt,
       start_t, tact, tact_for_player, x_cond;
  wire [1:0] adder_1_out, multiplexer_2_out, register_1_q;
  wire [2:0] random_1_out;
  wire [4:0] bitfinder_1_index, bitfinder_2_index, subtractor_1_out;
  wire [30:0] multiplexer_36_out, multiplexer_38_out, multiplexer_39_out, shifter_1_out, shifter_2_out,
       x_final, x_inverted_alt;
  wire [31:0] multiplexer_3_out, multiplexer_4_out, multiplexer_5_out, multiplexer_6_out, multiplexer_7_out,
       multiplexer_8_out, multiplexer_9_out, multiplexer_10_out, multiplexer_11_out, multiplexer_12_out,
       multiplexer_13_out, multiplexer_14_out, multiplexer_15_out, multiplexer_16_out, multiplexer_17_out,
       multiplexer_18_out, multiplexer_19_out, multiplexer_20_out, multiplexer_21_out, multiplexer_22_out,
       multiplexer_23_out, multiplexer_24_out, multiplexer_25_out, multiplexer_26_out, multiplexer_27_out,
       multiplexer_28_out, multiplexer_29_out, multiplexer_30_out, multiplexer_31_out, multiplexer_32_out,
       multiplexer_33_out, multiplexer_34_out, multiplexer_35_out, multiplexer_40_out, multiplexer_41_out,
       or_4_out, shifter_3_out, shifter_4_out, y_final;

  Clock clock_1 (.out(clock_1_out));
  Multiplexer #(.enable("false")) multiplexer_1 (
    .in0(clock_1_out), .in1(1'b0), .out(multiplexer_1_out), .sel(d_ff_2_q));
  Random #(.width(3)) random_1 (.clk(tact), .out(random_1_out));  // open: next, clr
  D_Flip_Flop d_ff_1 (.clk(multiplexer_1_out), .D(not_1_out), .Q(d_ff_1_q));  // open: Qn, preset, en, reset
  not not_1 (not_1_out, d_ff_1_q);
  D_Flip_Flop d_ff_2 (.clk(pause), .D(not_2_out), .Q(d_ff_2_q));  // open: Qn, preset, en, reset
  not not_2 (not_2_out, d_ff_2_q);
  Multiplexer #(.width(2), .enable("false")) multiplexer_2 (
    .in0(adder_1_out), .in1(2'b00), .out(multiplexer_2_out), .sel(start_t));
  not not_3 (start_t, start);
  D_Flip_Flop d_ff_3 (.clk(d_ff_1_q), .D(not_5_out), .Q(d_ff_3_q));  // open: Qn, preset, en, reset
  not not_4 (not_4_out, d_ff_4_q);
  not not_5 (not_5_out, d_ff_3_q);
  Multiplexer #(.select(3), .width(32), .enable("false")) multiplexer_3 (
    .in0(32'hfe3ffff), .in1(32'h7fff8ff8), .in2(32'h78ffff1f), .in3(32'h7ffc7ff1), .in4(32'h7f1ff8ff),
    .in5(32'h7fffe3ff), .in6(32'h47fe3fff), .in7(32'h7ff8ffc7), .out(multiplexer_3_out), .sel(random_1_out));
  Register #(.width(2)) register_1 (.D(multiplexer_2_out), .Q(register_1_q), .clk(tact));  // open: en, clr
  Adder #(.width(2)) adder_1 (.a(register_1_q), .b(2'b01), .out(adder_1_out));  // open: cin, cout
  Multiplexer #(.width(32), .enable("false")) multiplexer_4 (
    .in0(out_7), .in1({32{1'b0}}), .out(multiplexer_4_out), .sel(start_t));
  Multiplexer #(.width(32), .enable("false")) multiplexer_5 (
    .in0(out_12), .in1(32'hfe3ffff), .out(multiplexer_5_out), .sel(start_t));
  Multiplexer #(.width(32), .enable("false")) multiplexer_6 (
    .in0(out_16), .in1({32{1'b0}}), .out(multiplexer_6_out), .sel(start_t));
  Multiplexer #(.width(32), .enable("false")) multiplexer_7 (
    .in0(out_20), .in1({32{1'b0}}), .out(multiplexer_7_out), .sel(start_t));
  Multiplexer #(.width(32), .enable("false")) multiplexer_8 (
    .in0(out_24), .in1({32{1'b0}}), .out(multiplexer_8_out), .sel(start_t));
  Multiplexer #(.width(32), .enable("false")) multiplexer_9 (
    .in0(out_28), .in1(32'h7fff8ff8), .out(multiplexer_9_out), .sel(start_t));
  Multiplexer #(.width(32), .enable("false")) multiplexer_10 (
    .in0(out_32), .in1({32{1'b0}}), .out(multiplexer_10_out), .sel(start_t));
  D_Flip_Flop d_ff_4 (.clk(d_ff_3_q), .D(not_4_out), .Q(d_ff_4_q));  // open: Qn, preset, en, reset
  not not_6 (not_6_out, d_ff_5_q);
  Register #(.width(32)) register_2 (.D(multiplexer_3_out), .en(start_alt), .Q(out_7), .clk(tact), .clr(or_1_out));
  or or_1 (or_1_out, not_7_out, start_t);
  not not_7 (not_7_out, adder_1_out[1]);
  Register #(.width(32)) register_3 (.D(multiplexer_4_out), .en(start_alt), .Q(out_12), .clk(tact));  // open: clr
  Register #(.width(32)) register_4 (.D(multiplexer_5_out), .en(start_alt), .Q(out_16), .clk(tact));  // open: clr
  Register #(.width(32)) register_5 (.D(multiplexer_6_out), .en(start_alt), .Q(out_20), .clk(tact));  // open: clr
  Register #(.width(32)) register_6 (.D(multiplexer_7_out), .en(start_alt), .Q(out_24), .clk(tact));  // open: clr
  Register #(.width(32)) register_7 (.D(multiplexer_8_out), .en(start_alt), .Q(out_28), .clk(tact));  // open: clr
  Register #(.width(32)) register_8 (.D(multiplexer_9_out), .en(start_alt), .Q(out_32), .clk(tact));  // open: clr
  Register #(.width(32)) register_9 (.D(multiplexer_10_out), .en(start_alt), .Q(out_36), .clk(tact));  // open: clr
  D_Flip_Flop d_ff_5 (.clk(d_ff_4_q), .D(not_6_out), .Q(d_ff_5_q));  // open: Qn, preset, en, reset
  not not_8 (not_8_out, tact_for_player);
  D_Flip_Flop d_ff_6 (.clk(tact_for_player), .D(not_9_out), .Q(tact));  // open: Qn, preset, en, reset
  D_Flip_Flop d_ff_7 (.clk(d_ff_5_q), .D(not_8_out), .Q(tact_for_player));  // open: Qn, preset, en, reset
  not not_9 (not_9_out, tact);
  Multiplexer #(.width(32), .enable("false")) multiplexer_11 (
    .in0(out_36), .in1({32{1'b0}}), .out(multiplexer_11_out), .sel(start_t));
  Register #(.width(32)) register_10 (.D(multiplexer_11_out), .en(start_alt), .Q(out_8), .clk(tact));  // open: clr
  Multiplexer #(.width(32), .enable("false")) multiplexer_12 (
    .in0(out_8), .in1({32{1'b0}}), .out(multiplexer_12_out), .sel(start_t));
  Register #(.width(32)) register_11 (.D(multiplexer_12_out), .en(start_alt), .Q(out_13), .clk(tact));  // open: clr
  Register #(.width(32)) register_12 (.D(multiplexer_13_out), .en(start_alt), .Q(out_17), .clk(tact));  // open: clr
  Multiplexer #(.width(32), .enable("false")) multiplexer_13 (
    .in0(out_13), .in1(32'h78ffff1f), .out(multiplexer_13_out), .sel(start_t));
  Register #(.width(32)) register_13 (.D(multiplexer_14_out), .en(start_alt), .Q(out_21), .clk(tact));  // open: clr
  Multiplexer #(.width(32), .enable("false")) multiplexer_14 (
    .in0(out_17), .in1({32{1'b0}}), .out(multiplexer_14_out), .sel(start_t));
  Register #(.width(32)) register_14 (.D(multiplexer_15_out), .en(start_alt), .Q(out_25), .clk(tact));  // open: clr
  Multiplexer #(.width(32), .enable("false")) multiplexer_15 (
    .in0(out_21), .in1({32{1'b0}}), .out(multiplexer_15_out), .sel(start_t));
  Register #(.width(32)) register_15 (.D(multiplexer_16_out), .en(start_alt), .Q(out_29), .clk(tact));  // open: clr
  Multiplexer #(.width(32), .enable("false")) multiplexer_16 (
    .in0(out_25), .in1({32{1'b0}}), .out(multiplexer_16_out), .sel(start_t));
  Register #(.width(32)) register_16 (.D(multiplexer_17_out), .en(start_alt), .Q(out_33), .clk(tact));  // open: clr
  Multiplexer #(.width(32), .enable("false")) multiplexer_17 (
    .in0(out_29), .in1(32'h7ffc7ff1), .out(multiplexer_17_out), .sel(start_t));
  Register #(.width(32)) register_17 (.D(multiplexer_18_out), .en(start_alt), .Q(out_37), .clk(tact));  // open: clr
  Multiplexer #(.width(32), .enable("false")) multiplexer_18 (
    .in0(out_33), .in1({32{1'b0}}), .out(multiplexer_18_out), .sel(start_t));
  Multiplexer #(.width(32), .enable("false")) multiplexer_19 (
    .in0(out_37), .in1({32{1'b0}}), .out(multiplexer_19_out), .sel(start_t));
  Multiplexer #(.width(32), .enable("false")) multiplexer_20 (
    .in0(out_9), .in1({32{1'b0}}), .out(multiplexer_20_out), .sel(start_t));
  Multiplexer #(.width(32), .enable("false")) multiplexer_21 (
    .in0(out_14), .in1(32'h7ff8ffc7), .out(multiplexer_21_out), .sel(start_t));
  Multiplexer #(.width(32), .enable("false")) multiplexer_22 (
    .in0(out_18), .in1({32{1'b0}}), .out(multiplexer_22_out), .sel(start_t));
  Multiplexer #(.width(32), .enable("false")) multiplexer_23 (
    .in0(out_22), .in1({32{1'b0}}), .out(multiplexer_23_out), .sel(start_t));
  Multiplexer #(.width(32), .enable("false")) multiplexer_24 (
    .in0(out_26), .in1({32{1'b0}}), .out(multiplexer_24_out), .sel(start_t));
  Multiplexer #(.width(32), .enable("false")) multiplexer_25 (
    .in0(out_30), .in1(32'h7fffe3ff), .out(multiplexer_25_out), .sel(start_t));
  Multiplexer #(.width(32), .enable("false")) multiplexer_26 (
    .in0(out_34), .in1({32{1'b0}}), .out(multiplexer_26_out), .sel(start_t));
  Register #(.width(32)) register_18 (.D(multiplexer_19_out), .en(start_alt), .Q(out_9), .clk(tact));  // open: clr
  Register #(.width(32)) register_19 (.D(multiplexer_20_out), .en(start_alt), .Q(out_14), .clk(tact));  // open: clr
  Register #(.width(32)) register_20 (.D(multiplexer_21_out), .en(start_alt), .Q(out_18), .clk(tact));  // open: clr
  Register #(.width(32)) register_21 (.D(multiplexer_22_out), .en(start_alt), .Q(out_22), .clk(tact));  // open: clr
  Register #(.width(32)) register_22 (.D(multiplexer_23_out), .en(start_alt), .Q(out_26), .clk(tact));  // open: clr
  Register #(.width(32)) register_23 (.D(multiplexer_24_out), .en(start_alt), .Q(out_30), .clk(tact));  // open: clr
  Register #(.width(32)) register_24 (.D(multiplexer_25_out), .en(start_alt), .Q(out_34), .clk(tact));  // open: clr
  Register #(.width(32)) register_25 (.D(multiplexer_26_out), .en(start_alt), .Q(out_38), .clk(tact));  // open: clr
  DotMatrix #(.inputtype("row"), .matrixcols(32), .matrixrows(16)) dotmatrix_1 (
    .row0(32'hfe3ffff), .row1(32'h7fff8ff8), .row2(32'h78ffff1f), .row3(32'h7ffc7ff1), .row4(32'h7f1ff8ff),
    .row5(32'h7fffe3ff), .row6(32'h47fe3fff), .row7(32'h7ff8ffc7));  // open: row8, row9, row10, row11, row12, row13, row14, row15
  Register #(.width(32)) register_26 (.D(multiplexer_27_out), .en(start_alt), .Q(out_10), .clk(tact));  // open: clr
  Multiplexer #(.width(32), .enable("false")) multiplexer_27 (
    .in0(out_38), .in1({32{1'b0}}), .out(multiplexer_27_out), .sel(start_t));
  Multiplexer #(.width(32), .enable("false")) multiplexer_28 (
    .in0(out_10), .in1({32{1'b0}}), .out(multiplexer_28_out), .sel(start_t));
  Register #(.width(32)) register_27 (.D(multiplexer_28_out), .en(start_alt), .Q(out_15), .clk(tact));  // open: clr
  Register #(.width(32)) register_28 (.D(multiplexer_29_out), .en(start_alt), .Q(out_19), .clk(tact));  // open: clr
  Multiplexer #(.width(32), .enable("false")) multiplexer_29 (
    .in0(out_15), .in1(32'h47fe3fff), .out(multiplexer_29_out), .sel(start_t));
  Register #(.width(32)) register_29 (.D(multiplexer_30_out), .en(start_alt), .Q(out_23), .clk(tact));  // open: clr
  Multiplexer #(.width(32), .enable("false")) multiplexer_30 (
    .in0(out_19), .in1({32{1'b0}}), .out(multiplexer_30_out), .sel(start_t));
  Register #(.width(32)) register_30 (.D(multiplexer_31_out), .en(start_alt), .Q(out_27), .clk(tact));  // open: clr
  Multiplexer #(.width(32), .enable("false")) multiplexer_31 (
    .in0(out_23), .in1({32{1'b0}}), .out(multiplexer_31_out), .sel(start_t));
  Register #(.width(32)) register_31 (.D(multiplexer_32_out), .en(start_alt), .Q(out_31), .clk(tact));  // open: clr
  Multiplexer #(.width(32), .enable("false")) multiplexer_32 (
    .in0(out_27), .in1({32{1'b0}}), .out(multiplexer_32_out), .sel(start_t));
  Register #(.width(32)) register_32 (.D(multiplexer_33_out), .en(start_alt), .Q(out_35), .clk(tact));  // open: clr
  Multiplexer #(.width(32), .enable("false")) multiplexer_33 (
    .in0(out_31), .in1(32'h7f1ff8ff), .out(multiplexer_33_out), .sel(start_t));
  Multiplexer #(.width(32), .enable("false")) multiplexer_34 (
    .in0(out_35), .in1({32{1'b0}}), .out(multiplexer_34_out), .sel(start_t));
  Register #(.width(32)) register_33 (.D(multiplexer_34_out), .en(start_alt), .Q(out_39), .clk(tact));  // open: clr
  Multiplexer #(.width(32), .enable("false")) multiplexer_35 (
    .in0(32'h1800000), .in1(y_final), .out(multiplexer_35_out), .sel(start));
  Register #(.width(31)) register_34 (.D(multiplexer_36_out), .Q(out_5), .clk(tact_for_player));  // open: en, clr
  Multiplexer #(.width(31), .enable("false")) multiplexer_36 (
    .in0(31'hc000), .in1(x_final), .out(multiplexer_36_out), .sel(start));
  Register #(.width(32)) register_35 (.D(multiplexer_35_out), .Q(out_6), .clk(tact));  // open: en, clr
  check_helper check_helper_1 (.in_1(out_7), .in_2({1'b0, x_inverted_alt}), .out_3(check_helper_1_out_3));
  check_helper check_helper_2 (.in_1(out_12), .in_2({1'b0, x_inverted_alt}), .out_3(check_helper_2_out_3));
  check_helper check_helper_3 (.in_1(out_16), .in_2({1'b0, x_inverted_alt}), .out_3(check_helper_3_out_3));
  check_helper check_helper_4 (.in_1(out_20), .in_2({1'b0, x_inverted_alt}), .out_3(check_helper_4_out_3));
  check_helper check_helper_5 (.in_1(out_24), .in_2({1'b0, x_inverted_alt}), .out_3(check_helper_5_out_3));
  check_helper check_helper_6 (.in_1(out_28), .in_2({1'b0, x_inverted_alt}), .out_3(check_helper_6_out_3));
  check_helper check_helper_7 (.in_1(out_32), .in_2({1'b0, x_inverted_alt}), .out_3(check_helper_7_out_3));
  check_helper check_helper_8 (.in_1(out_36), .in_2({1'b0, x_inverted_alt}), .out_3(check_helper_8_out_3));
  check_helper check_helper_9 (.in_1(out_8), .in_2({1'b0, x_inverted_alt}), .out_3(check_helper_9_out_3));
  check_helper check_helper_10 (.in_1(out_13), .in_2({1'b0, x_inverted_alt}), .out_3(check_helper_10_out_3));
  check_helper check_helper_11 (.in_1(out_17), .in_2({1'b0, x_inverted_alt}), .out_3(check_helper_11_out_3));
  check_helper check_helper_12 (.in_1(out_21), .in_2({1'b0, x_inverted_alt}), .out_3(check_helper_12_out_3));
  check_helper check_helper_13 (.in_1(out_25), .in_2({1'b0, x_inverted_alt}), .out_3(check_helper_13_out_3));
  check_helper check_helper_14 (.in_1(out_29), .in_2({1'b0, x_inverted_alt}), .out_3(check_helper_14_out_3));
  check_helper check_helper_15 (.in_1(out_33), .in_2({1'b0, x_inverted_alt}), .out_3(check_helper_15_out_3));
  check_helper check_helper_16 (.in_1(out_37), .in_2({1'b0, x_inverted_alt}), .out_3(check_helper_16_out_3));
  Multiplexer #(.select(5), .enable("false")) multiplexer_37 (
    .in0(check_helper_1_out_3), .in1(check_helper_2_out_3), .in2(check_helper_3_out_3),
    .in3(check_helper_4_out_3), .in4(check_helper_5_out_3), .in5(check_helper_6_out_3),
    .in6(check_helper_7_out_3), .in7(check_helper_8_out_3), .in8(check_helper_9_out_3),
    .in9(check_helper_10_out_3), .in10(check_helper_11_out_3), .in11(check_helper_12_out_3),
    .in12(check_helper_13_out_3), .in13(check_helper_14_out_3), .in14(check_helper_15_out_3),
    .in15(check_helper_16_out_3), .in16(check_helper_17_out_3), .in17(check_helper_18_out_3),
    .in18(check_helper_19_out_3), .in19(check_helper_20_out_3), .in20(check_helper_21_out_3),
    .in21(check_helper_22_out_3), .in22(check_helper_23_out_3), .in23(check_helper_24_out_3),
    .in24(check_helper_25_out_3), .in25(check_helper_26_out_3), .in26(check_helper_27_out_3),
    .in27(check_helper_28_out_3), .in28(check_helper_29_out_3), .in29(check_helper_30_out_3),
    .in30(check_helper_31_out_3), .in31(check_helper_32_out_3), .out(x_cond), .sel(bitfinder_1_index));
  check_helper check_helper_17 (.in_1(out_9), .in_2({1'b0, x_inverted_alt}), .out_3(check_helper_17_out_3));
  check_helper check_helper_18 (.in_1(out_14), .in_2({1'b0, x_inverted_alt}), .out_3(check_helper_18_out_3));
  check_helper check_helper_19 (.in_1(out_18), .in_2({1'b0, x_inverted_alt}), .out_3(check_helper_19_out_3));
  check_helper check_helper_20 (.in_1(out_22), .in_2({1'b0, x_inverted_alt}), .out_3(check_helper_20_out_3));
  check_helper check_helper_21 (.in_1(out_26), .in_2({1'b0, x_inverted_alt}), .out_3(check_helper_21_out_3));
  check_helper check_helper_22 (.in_1(out_30), .in_2({1'b0, x_inverted_alt}), .out_3(check_helper_22_out_3));
  check_helper check_helper_23 (.in_1(out_34), .in_2({1'b0, x_inverted_alt}), .out_3(check_helper_23_out_3));
  check_helper check_helper_24 (.in_1(out_38), .in_2({1'b0, x_inverted_alt}), .out_3(check_helper_24_out_3));
  check_helper check_helper_25 (.in_1(out_10), .in_2({1'b0, x_inverted_alt}), .out_3(check_helper_25_out_3));
  check_helper check_helper_26 (.in_1(out_15), .in_2({1'b0, x_inverted_alt}), .out_3(check_helper_26_out_3));
  check_helper check_helper_27 (.in_1(out_19), .in_2({1'b0, x_inverted_alt}), .out_3(check_helper_27_out_3));
  check_helper check_helper_28 (.in_1(out_23), .in_2({1'b0, x_inverted_alt}), .out_3(check_helper_28_out_3));
  check_helper check_helper_29 (.in_1(out_27), .in_2({1'b0, x_inverted_alt}), .out_3(check_helper_29_out_3));
  check_helper check_helper_30 (.in_1(out_31), .in_2({1'b0, x_inverted_alt}), .out_3(check_helper_30_out_3));
  check_helper check_helper_31 (.in_1(out_35), .in_2({1'b0, x_inverted_alt}), .out_3(check_helper_31_out_3));
  check_helper check_helper_32 (.in_1(out_39), .in_2({1'b0, x_inverted_alt}), .out_3(check_helper_32_out_3));
  BitFinder #(.width(32), .\type ("high1")) bitfinder_1 (.in(out_6), .index(bitfinder_1_index));  // open: found
  Multiplexer #(.width(31), .enable("false")) multiplexer_38 (
    .in0({31{1'b0}}), .in1(shifter_1_out), .out(multiplexer_38_out), .sel(x_left));
  Shifter #(.width(31), .shift("lr")) shifter_1 (.in(out_5), .\dist (5'b00001), .out(shifter_1_out));
  Multiplexer #(.width(31), .enable("false")) multiplexer_39 (
    .in0({31{1'b0}}), .in1(shifter_2_out), .out(multiplexer_39_out), .sel(x_right));
  Shifter #(.width(31)) shifter_2 (.in(out_5), .\dist (5'b00001), .out(shifter_2_out));
  Shifter #(.width(32), .shift("lr")) shifter_3 (.in(out_6), .\dist (5'b00001), .out(shifter_3_out));
  Shifter #(.width(32)) shifter_4 (.in(out_6), .\dist (5'b00001), .out(shifter_4_out));
  not not_10 (not_10_out, down);
  assign {x_inverted_alt[0], x_inverted_alt[1], x_inverted_alt[2], x_inverted_alt[3], x_inverted_alt[4], x_inverted_alt[5], x_inverted_alt[6], x_inverted_alt[7], x_inverted_alt[8], x_inverted_alt[9], x_inverted_alt[10], x_inverted_alt[11], x_inverted_alt[12], x_inverted_alt[13], x_inverted_alt[14], x_inverted_alt[15], x_inverted_alt[16], x_inverted_alt[17], x_inverted_alt[18], x_inverted_alt[19], x_inverted_alt[20], x_inverted_alt[21], x_inverted_alt[22], x_inverted_alt[23], x_inverted_alt[24], x_inverted_alt[25], x_inverted_alt[26], x_inverted_alt[27], x_inverted_alt[28], x_inverted_alt[29], x_inverted_alt[30]} = multiplexer_38_out | multiplexer_39_out;  // OR_Gate or_2, 31 bits wide
  not not_11 (not_11_out, x_inverted_alt[0]);
  or or_3 (or_3_out, not_11_out, x_inverted_alt[1]);
  Multiplexer #(.width(32), .enable("false")) multiplexer_40 (
    .in0({32{1'b0}}), .in1(shifter_3_out), .out(multiplexer_40_out), .sel(down));
  assign or_4_out = multiplexer_40_out | multiplexer_41_out;  // OR_Gate or_4, 32 bits wide
  Multiplexer #(.width(32), .enable("false")) multiplexer_41 (
    .in0({32{1'b0}}), .in1(shifter_4_out), .out(multiplexer_41_out), .sel(not_10_out));
  not not_12 (not_12_out, x_inverted_alt[30]);
  or or_5 (or_5_out, not_12_out, x_inverted_alt[29]);
  not not_13 (not_13_out, or_4_out[0]);
  or or_6 (or_6_out, not_13_out, or_4_out[1]);
  Multiplexer #(.width(31), .enable("false")) multiplexer_42 (
    .in0(out_5),
    .in1({x_inverted_alt[0], x_inverted_alt[1], x_inverted_alt[2], x_inverted_alt[3], x_inverted_alt[4], x_inverted_alt[5], x_inverted_alt[6], x_inverted_alt[7], x_inverted_alt[8], x_inverted_alt[9], x_inverted_alt[10], x_inverted_alt[11], x_inverted_alt[12], x_inverted_alt[13], x_inverted_alt[14], x_inverted_alt[15], x_inverted_alt[16], x_inverted_alt[17], x_inverted_alt[18], x_inverted_alt[19], x_inverted_alt[20], x_inverted_alt[21], x_inverted_alt[22], x_inverted_alt[23], x_inverted_alt[24], x_inverted_alt[25], x_inverted_alt[26], x_inverted_alt[27], x_inverted_alt[28], x_inverted_alt[29], x_inverted_alt[30]}),
    .out(x_final), .sel(and_1_out));
  and and_1 (and_1_out, x_cond, or_5_out, or_3_out, not_14_out);
  not not_14 (not_14_out, comparator_1_eq);
  Comparator #(.width(31)) comparator_1 (
    .a({x_inverted_alt[0], x_inverted_alt[1], x_inverted_alt[2], x_inverted_alt[3], x_inverted_alt[4], x_inverted_alt[5], x_inverted_alt[6], x_inverted_alt[7], x_inverted_alt[8], x_inverted_alt[9], x_inverted_alt[10], x_inverted_alt[11], x_inverted_alt[12], x_inverted_alt[13], x_inverted_alt[14], x_inverted_alt[15], x_inverted_alt[16], x_inverted_alt[17], x_inverted_alt[18], x_inverted_alt[19], x_inverted_alt[20], x_inverted_alt[21], x_inverted_alt[22], x_inverted_alt[23], x_inverted_alt[24], x_inverted_alt[25], x_inverted_alt[26], x_inverted_alt[27], x_inverted_alt[28], x_inverted_alt[29], x_inverted_alt[30]}),
    .b({31{1'b0}}), .eq(comparator_1_eq));  // open: gt, lt
  Multiplexer #(.width(32), .enable("false")) multiplexer_43 (
    .in0(out_6), .in1(or_4_out), .out(y_final), .sel(and_2_out));
  and and_2 (and_2_out, or_6_out, not_15_out);
  not not_15 (not_15_out, comparator_2_eq);
  Comparator #(.width(32)) comparator_2 (.a(or_4_out), .b({32{1'b0}}), .eq(comparator_2_eq));  // open: gt, lt
  check_helper check_helper_33 (
    .in_1(out_7),
    .in_2({1'b0, x_final[0], x_final[1], x_final[2], x_final[3], x_final[4], x_final[5], x_final[6], x_final[7], x_final[8], x_final[9], x_final[10], x_final[11], x_final[12], x_final[13], x_final[14], x_final[15], x_final[16], x_final[17], x_final[18], x_final[19], x_final[20], x_final[21], x_final[22], x_final[23], x_final[24], x_final[25], x_final[26], x_final[27], x_final[28], x_final[29], x_final[30]}),
    .out_3(check_helper_33_out_3));
  check_helper check_helper_34 (
    .in_1(out_12),
    .in_2({1'b0, x_final[0], x_final[1], x_final[2], x_final[3], x_final[4], x_final[5], x_final[6], x_final[7], x_final[8], x_final[9], x_final[10], x_final[11], x_final[12], x_final[13], x_final[14], x_final[15], x_final[16], x_final[17], x_final[18], x_final[19], x_final[20], x_final[21], x_final[22], x_final[23], x_final[24], x_final[25], x_final[26], x_final[27], x_final[28], x_final[29], x_final[30]}),
    .out_3(check_helper_34_out_3));
  check_helper check_helper_35 (
    .in_1(out_16),
    .in_2({1'b0, x_final[0], x_final[1], x_final[2], x_final[3], x_final[4], x_final[5], x_final[6], x_final[7], x_final[8], x_final[9], x_final[10], x_final[11], x_final[12], x_final[13], x_final[14], x_final[15], x_final[16], x_final[17], x_final[18], x_final[19], x_final[20], x_final[21], x_final[22], x_final[23], x_final[24], x_final[25], x_final[26], x_final[27], x_final[28], x_final[29], x_final[30]}),
    .out_3(check_helper_35_out_3));
  check_helper check_helper_36 (
    .in_1(out_20),
    .in_2({1'b0, x_final[0], x_final[1], x_final[2], x_final[3], x_final[4], x_final[5], x_final[6], x_final[7], x_final[8], x_final[9], x_final[10], x_final[11], x_final[12], x_final[13], x_final[14], x_final[15], x_final[16], x_final[17], x_final[18], x_final[19], x_final[20], x_final[21], x_final[22], x_final[23], x_final[24], x_final[25], x_final[26], x_final[27], x_final[28], x_final[29], x_final[30]}),
    .out_3(check_helper_36_out_3));
  check_helper check_helper_37 (
    .in_1(out_24),
    .in_2({1'b0, x_final[0], x_final[1], x_final[2], x_final[3], x_final[4], x_final[5], x_final[6], x_final[7], x_final[8], x_final[9], x_final[10], x_final[11], x_final[12], x_final[13], x_final[14], x_final[15], x_final[16], x_final[17], x_final[18], x_final[19], x_final[20], x_final[21], x_final[22], x_final[23], x_final[24], x_final[25], x_final[26], x_final[27], x_final[28], x_final[29], x_final[30]}),
    .out_3(check_helper_37_out_3));
  check_helper check_helper_38 (
    .in_1(out_28),
    .in_2({1'b0, x_final[0], x_final[1], x_final[2], x_final[3], x_final[4], x_final[5], x_final[6], x_final[7], x_final[8], x_final[9], x_final[10], x_final[11], x_final[12], x_final[13], x_final[14], x_final[15], x_final[16], x_final[17], x_final[18], x_final[19], x_final[20], x_final[21], x_final[22], x_final[23], x_final[24], x_final[25], x_final[26], x_final[27], x_final[28], x_final[29], x_final[30]}),
    .out_3(check_helper_38_out_3));
  check_helper check_helper_39 (
    .in_1(out_32),
    .in_2({1'b0, x_final[0], x_final[1], x_final[2], x_final[3], x_final[4], x_final[5], x_final[6], x_final[7], x_final[8], x_final[9], x_final[10], x_final[11], x_final[12], x_final[13], x_final[14], x_final[15], x_final[16], x_final[17], x_final[18], x_final[19], x_final[20], x_final[21], x_final[22], x_final[23], x_final[24], x_final[25], x_final[26], x_final[27], x_final[28], x_final[29], x_final[30]}),
    .out_3(check_helper_39_out_3));
  check_helper check_helper_40 (
    .in_1(out_36),
    .in_2({1'b0, x_final[0], x_final[1], x_final[2], x_final[3], x_final[4], x_final[5], x_final[6], x_final[7], x_final[8], x_final[9], x_final[10], x_final[11], x_final[12], x_final[13], x_final[14], x_final[15], x_final[16], x_final[17], x_final[18], x_final[19], x_final[20], x_final[21], x_final[22], x_final[23], x_final[24], x_final[25], x_final[26], x_final[27], x_final[28], x_final[29], x_final[30]}),
    .out_3(check_helper_40_out_3));
  check_helper check_helper_41 (
    .in_1(out_8),
    .in_2({1'b0, x_final[0], x_final[1], x_final[2], x_final[3], x_final[4], x_final[5], x_final[6], x_final[7], x_final[8], x_final[9], x_final[10], x_final[11], x_final[12], x_final[13], x_final[14], x_final[15], x_final[16], x_final[17], x_final[18], x_final[19], x_final[20], x_final[21], x_final[22], x_final[23], x_final[24], x_final[25], x_final[26], x_final[27], x_final[28], x_final[29], x_final[30]}),
    .out_3(check_helper_41_out_3));
  check_helper check_helper_42 (
    .in_1(out_13),
    .in_2({1'b0, x_final[0], x_final[1], x_final[2], x_final[3], x_final[4], x_final[5], x_final[6], x_final[7], x_final[8], x_final[9], x_final[10], x_final[11], x_final[12], x_final[13], x_final[14], x_final[15], x_final[16], x_final[17], x_final[18], x_final[19], x_final[20], x_final[21], x_final[22], x_final[23], x_final[24], x_final[25], x_final[26], x_final[27], x_final[28], x_final[29], x_final[30]}),
    .out_3(check_helper_42_out_3));
  check_helper check_helper_43 (
    .in_1(out_17),
    .in_2({1'b0, x_final[0], x_final[1], x_final[2], x_final[3], x_final[4], x_final[5], x_final[6], x_final[7], x_final[8], x_final[9], x_final[10], x_final[11], x_final[12], x_final[13], x_final[14], x_final[15], x_final[16], x_final[17], x_final[18], x_final[19], x_final[20], x_final[21], x_final[22], x_final[23], x_final[24], x_final[25], x_final[26], x_final[27], x_final[28], x_final[29], x_final[30]}),
    .out_3(check_helper_43_out_3));
  check_helper check_helper_44 (
    .in_1(out_21),
    .in_2({1'b0, x_final[0], x_final[1], x_final[2], x_final[3], x_final[4], x_final[5], x_final[6], x_final[7], x_final[8], x_final[9], x_final[10], x_final[11], x_final[12], x_final[13], x_final[14], x_final[15], x_final[16], x_final[17], x_final[18], x_final[19], x_final[20], x_final[21], x_final[22], x_final[23], x_final[24], x_final[25], x_final[26], x_final[27], x_final[28], x_final[29], x_final[30]}),
    .out_3(check_helper_44_out_3));
  check_helper check_helper_45 (
    .in_1(out_25),
    .in_2({1'b0, x_final[0], x_final[1], x_final[2], x_final[3], x_final[4], x_final[5], x_final[6], x_final[7], x_final[8], x_final[9], x_final[10], x_final[11], x_final[12], x_final[13], x_final[14], x_final[15], x_final[16], x_final[17], x_final[18], x_final[19], x_final[20], x_final[21], x_final[22], x_final[23], x_final[24], x_final[25], x_final[26], x_final[27], x_final[28], x_final[29], x_final[30]}),
    .out_3(check_helper_45_out_3));
  check_helper check_helper_46 (
    .in_1(out_29),
    .in_2({1'b0, x_final[0], x_final[1], x_final[2], x_final[3], x_final[4], x_final[5], x_final[6], x_final[7], x_final[8], x_final[9], x_final[10], x_final[11], x_final[12], x_final[13], x_final[14], x_final[15], x_final[16], x_final[17], x_final[18], x_final[19], x_final[20], x_final[21], x_final[22], x_final[23], x_final[24], x_final[25], x_final[26], x_final[27], x_final[28], x_final[29], x_final[30]}),
    .out_3(check_helper_46_out_3));
  check_helper check_helper_47 (
    .in_1(out_33),
    .in_2({1'b0, x_final[0], x_final[1], x_final[2], x_final[3], x_final[4], x_final[5], x_final[6], x_final[7], x_final[8], x_final[9], x_final[10], x_final[11], x_final[12], x_final[13], x_final[14], x_final[15], x_final[16], x_final[17], x_final[18], x_final[19], x_final[20], x_final[21], x_final[22], x_final[23], x_final[24], x_final[25], x_final[26], x_final[27], x_final[28], x_final[29], x_final[30]}),
    .out_3(check_helper_47_out_3));
  check_helper check_helper_48 (
    .in_1(out_37),
    .in_2({1'b0, x_final[0], x_final[1], x_final[2], x_final[3], x_final[4], x_final[5], x_final[6], x_final[7], x_final[8], x_final[9], x_final[10], x_final[11], x_final[12], x_final[13], x_final[14], x_final[15], x_final[16], x_final[17], x_final[18], x_final[19], x_final[20], x_final[21], x_final[22], x_final[23], x_final[24], x_final[25], x_final[26], x_final[27], x_final[28], x_final[29], x_final[30]}),
    .out_3(check_helper_48_out_3));
  Multiplexer #(.select(5), .enable("false")) multiplexer_44 (
    .in0(check_helper_33_out_3), .in1(check_helper_34_out_3), .in2(check_helper_35_out_3),
    .in3(check_helper_36_out_3), .in4(check_helper_37_out_3), .in5(check_helper_38_out_3),
    .in6(check_helper_39_out_3), .in7(check_helper_40_out_3), .in8(check_helper_41_out_3),
    .in9(check_helper_42_out_3), .in10(check_helper_43_out_3), .in11(check_helper_44_out_3),
    .in12(check_helper_45_out_3), .in13(check_helper_46_out_3), .in14(check_helper_47_out_3),
    .in15(check_helper_48_out_3), .in16(check_helper_49_out_3), .in17(check_helper_50_out_3),
    .in18(check_helper_51_out_3), .in19(check_helper_52_out_3), .in20(check_helper_53_out_3),
    .in21(check_helper_54_out_3), .in22(check_helper_55_out_3), .in23(check_helper_56_out_3),
    .in24(check_helper_57_out_3), .in25(check_helper_58_out_3), .in26(check_helper_59_out_3),
    .in27(check_helper_60_out_3), .in28(check_helper_61_out_3), .in29(check_helper_62_out_3),
    .in30(check_helper_63_out_3), .in31(check_helper_64_out_3), .out(multiplexer_44_out),
    .sel(subtractor_1_out));
  check_helper check_helper_49 (
    .in_1(out_9),
    .in_2({1'b0, x_final[0], x_final[1], x_final[2], x_final[3], x_final[4], x_final[5], x_final[6], x_final[7], x_final[8], x_final[9], x_final[10], x_final[11], x_final[12], x_final[13], x_final[14], x_final[15], x_final[16], x_final[17], x_final[18], x_final[19], x_final[20], x_final[21], x_final[22], x_final[23], x_final[24], x_final[25], x_final[26], x_final[27], x_final[28], x_final[29], x_final[30]}),
    .out_3(check_helper_49_out_3));
  check_helper check_helper_50 (
    .in_1(out_14),
    .in_2({1'b0, x_final[0], x_final[1], x_final[2], x_final[3], x_final[4], x_final[5], x_final[6], x_final[7], x_final[8], x_final[9], x_final[10], x_final[11], x_final[12], x_final[13], x_final[14], x_final[15], x_final[16], x_final[17], x_final[18], x_final[19], x_final[20], x_final[21], x_final[22], x_final[23], x_final[24], x_final[25], x_final[26], x_final[27], x_final[28], x_final[29], x_final[30]}),
    .out_3(check_helper_50_out_3));
  check_helper check_helper_51 (
    .in_1(out_18),
    .in_2({1'b0, x_final[0], x_final[1], x_final[2], x_final[3], x_final[4], x_final[5], x_final[6], x_final[7], x_final[8], x_final[9], x_final[10], x_final[11], x_final[12], x_final[13], x_final[14], x_final[15], x_final[16], x_final[17], x_final[18], x_final[19], x_final[20], x_final[21], x_final[22], x_final[23], x_final[24], x_final[25], x_final[26], x_final[27], x_final[28], x_final[29], x_final[30]}),
    .out_3(check_helper_51_out_3));
  check_helper check_helper_52 (
    .in_1(out_22),
    .in_2({1'b0, x_final[0], x_final[1], x_final[2], x_final[3], x_final[4], x_final[5], x_final[6], x_final[7], x_final[8], x_final[9], x_final[10], x_final[11], x_final[12], x_final[13], x_final[14], x_final[15], x_final[16], x_final[17], x_final[18], x_final[19], x_final[20], x_final[21], x_final[22], x_final[23], x_final[24], x_final[25], x_final[26], x_final[27], x_final[28], x_final[29], x_final[30]}),
    .out_3(check_helper_52_out_3));
  check_helper check_helper_53 (
    .in_1(out_26),
    .in_2({1'b0, x_final[0], x_final[1], x_final[2], x_final[3], x_final[4], x_final[5], x_final[6], x_final[7], x_final[8], x_final[9], x_final[10], x_final[11], x_final[12], x_final[13], x_final[14], x_final[15], x_final[16], x_final[17], x_final[18], x_final[19], x_final[20], x_final[21], x_final[22], x_final[23], x_final[24], x_final[25], x_final[26], x_final[27], x_final[28], x_final[29], x_final[30]}),
    .out_3(check_helper_53_out_3));
  check_helper check_helper_54 (
    .in_1(out_30),
    .in_2({1'b0, x_final[0], x_final[1], x_final[2], x_final[3], x_final[4], x_final[5], x_final[6], x_final[7], x_final[8], x_final[9], x_final[10], x_final[11], x_final[12], x_final[13], x_final[14], x_final[15], x_final[16], x_final[17], x_final[18], x_final[19], x_final[20], x_final[21], x_final[22], x_final[23], x_final[24], x_final[25], x_final[26], x_final[27], x_final[28], x_final[29], x_final[30]}),
    .out_3(check_helper_54_out_3));
  check_helper check_helper_55 (
    .in_1(out_34),
    .in_2({1'b0, x_final[0], x_final[1], x_final[2], x_final[3], x_final[4], x_final[5], x_final[6], x_final[7], x_final[8], x_final[9], x_final[10], x_final[11], x_final[12], x_final[13], x_final[14], x_final[15], x_final[16], x_final[17], x_final[18], x_final[19], x_final[20], x_final[21], x_final[22], x_final[23], x_final[24], x_final[25], x_final[26], x_final[27], x_final[28], x_final[29], x_final[30]}),
    .out_3(check_helper_55_out_3));
  check_helper check_helper_56 (
    .in_1(out_38),
    .in_2({1'b0, x_final[0], x_final[1], x_final[2], x_final[3], x_final[4], x_final[5], x_final[6], x_final[7], x_final[8], x_final[9], x_final[10], x_final[11], x_final[12], x_final[13], x_final[14], x_final[15], x_final[16], x_final[17], x_final[18], x_final[19], x_final[20], x_final[21], x_final[22], x_final[23], x_final[24], x_final[25], x_final[26], x_final[27], x_final[28], x_final[29], x_final[30]}),
    .out_3(check_helper_56_out_3));
  check_helper check_helper_57 (
    .in_1(out_10),
    .in_2({1'b0, x_final[0], x_final[1], x_final[2], x_final[3], x_final[4], x_final[5], x_final[6], x_final[7], x_final[8], x_final[9], x_final[10], x_final[11], x_final[12], x_final[13], x_final[14], x_final[15], x_final[16], x_final[17], x_final[18], x_final[19], x_final[20], x_final[21], x_final[22], x_final[23], x_final[24], x_final[25], x_final[26], x_final[27], x_final[28], x_final[29], x_final[30]}),
    .out_3(check_helper_57_out_3));
  check_helper check_helper_58 (
    .in_1(out_15),
    .in_2({1'b0, x_final[0], x_final[1], x_final[2], x_final[3], x_final[4], x_final[5], x_final[6], x_final[7], x_final[8], x_final[9], x_final[10], x_final[11], x_final[12], x_final[13], x_final[14], x_final[15], x_final[16], x_final[17], x_final[18], x_final[19], x_final[20], x_final[21], x_final[22], x_final[23], x_final[24], x_final[25], x_final[26], x_final[27], x_final[28], x_final[29], x_final[30]}),
    .out_3(check_helper_58_out_3));
  check_helper check_helper_59 (
    .in_1(out_19),
    .in_2({1'b0, x_final[0], x_final[1], x_final[2], x_final[3], x_final[4], x_final[5], x_final[6], x_final[7], x_final[8], x_final[9], x_final[10], x_final[11], x_final[12], x_final[13], x_final[14], x_final[15], x_final[16], x_final[17], x_final[18], x_final[19], x_final[20], x_final[21], x_final[22], x_final[23], x_final[24], x_final[25], x_final[26], x_final[27], x_final[28], x_final[29], x_final[30]}),
    .out_3(check_helper_59_out_3));
  check_helper check_helper_60 (
    .in_1(out_23),
    .in_2({1'b0, x_final[0], x_final[1], x_final[2], x_final[3], x_final[4], x_final[5], x_final[6], x_final[7], x_final[8], x_final[9], x_final[10], x_final[11], x_final[12], x_final[13], x_final[14], x_final[15], x_final[16], x_final[17], x_final[18], x_final[19], x_final[20], x_final[21], x_final[22], x_final[23], x_final[24], x_final[25], x_final[26], x_final[27], x_final[28], x_final[29], x_final[30]}),
    .out_3(check_helper_60_out_3));
  check_helper check_helper_61 (
    .in_1(out_27),
    .in_2({1'b0, x_final[0], x_final[1], x_final[2], x_final[3], x_final[4], x_final[5], x_final[6], x_final[7], x_final[8], x_final[9], x_final[10], x_final[11], x_final[12], x_final[13], x_final[14], x_final[15], x_final[16], x_final[17], x_final[18], x_final[19], x_final[20], x_final[21], x_final[22], x_final[23], x_final[24], x_final[25], x_final[26], x_final[27], x_final[28], x_final[29], x_final[30]}),
    .out_3(check_helper_61_out_3));
  check_helper check_helper_62 (
    .in_1(out_31),
    .in_2({1'b0, x_final[0], x_final[1], x_final[2], x_final[3], x_final[4], x_final[5], x_final[6], x_final[7], x_final[8], x_final[9], x_final[10], x_final[11], x_final[12], x_final[13], x_final[14], x_final[15], x_final[16], x_final[17], x_final[18], x_final[19], x_final[20], x_final[21], x_final[22], x_final[23], x_final[24], x_final[25], x_final[26], x_final[27], x_final[28], x_final[29], x_final[30]}),
    .out_3(check_helper_62_out_3));
  check_helper check_helper_63 (
    .in_1(out_35),
    .in_2({1'b0, x_final[0], x_final[1], x_final[2], x_final[3], x_final[4], x_final[5], x_final[6], x_final[7], x_final[8], x_final[9], x_final[10], x_final[11], x_final[12], x_final[13], x_final[14], x_final[15], x_final[16], x_final[17], x_final[18], x_final[19], x_final[20], x_final[21], x_final[22], x_final[23], x_final[24], x_final[25], x_final[26], x_final[27], x_final[28], x_final[29], x_final[30]}),
    .out_3(check_helper_63_out_3));
  check_helper check_helper_64 (
    .in_1(out_39),
    .in_2({1'b0, x_final[0], x_final[1], x_final[2], x_final[3], x_final[4], x_final[5], x_final[6], x_final[7], x_final[8], x_final[9], x_final[10], x_final[11], x_final[12], x_final[13], x_final[14], x_final[15], x_final[16], x_final[17], x_final[18], x_final[19], x_final[20], x_final[21], x_final[22], x_final[23], x_final[24], x_final[25], x_final[26], x_final[27], x_final[28], x_final[29], x_final[30]}),
    .out_3(check_helper_64_out_3));
  BitFinder #(.width(32)) bitfinder_2 (.in(out_6), .index(bitfinder_2_index));  // open: found
  Subtractor #(.width(5)) subtractor_1 (
    .a(bitfinder_2_index), .b(5'b00001), .out(subtractor_1_out));  // open: bin, bout
  Multiplexer #(.enable("false")) multiplexer_45 (.in0(1'b0), .in1(multiplexer_44_out), .out(down), .sel(start));
  DotMatrix #(.inputtype("row"), .matrixcols(32), .matrixrows(32)) dotmatrix_2 (
    .row0(out_39), .row1(out_35), .row2(out_31), .row3(out_27), .row4(out_23), .row5(out_19), .row6(out_15),
    .row7(out_10), .row8(out_38), .row9(out_34), .row10(out_30), .row11(out_26), .row12(out_22),
    .row13(out_18), .row14(out_14), .row15(out_9), .row16(out_37), .row17(out_33), .row18(out_29),
    .row19(out_25), .row20(out_21), .row21(out_17), .row22(out_13), .row23(out_8), .row24(out_36),
    .row25(out_32), .row26(out_28), .row27(out_24), .row28(out_20), .row29(out_16), .row30(out_12),
    .row31(out_7));
  // DotMatrix #(.inputtype("select"), .matrixcols(31), .matrixrows(32)) dotmatrix_3: pin names not known; wires that end beside it: out_5, out_6
  not not_16 (Lose, or_7_out);
  or or_7 (or_7_out, not_17_out, out_6[30]);
  not not_17 (not_17_out, out_6[31]);

  // Other names for the same wires on the sheet: _1[31:0] = out_7; _2[31:0] = out_12; _3[31:0] = out_16;
  //   _4[31:0] = out_20; _5[31:0] = out_24; _6[31:0] = out_28; _7[31:0] = out_32; _8[31:0] = out_36; _9[31:0] = out_8;
  //   _10[31:0] = out_13; _11[31:0] = out_17; _12[31:0] = out_21; _13[31:0] = out_25; _14[31:0] = out_29;
  //   _15[31:0] = out_33; _16[31:0] = out_37; _17[31:0] = out_9; _18[31:0] = out_14; _19[31:0] = out_18;
  //   _20[31:0] = out_22; _21[31:0] = out_26; _22[31:0] = out_30; _23[31:0] = out_34; _24[31:0] = out_38;
  //   _25[31:0] = out_10; _26[31:0] = out_15; _27[31:0] = out_19; _28[31:0] = out_23; _29[31:0] = out_27;
  //   _30[31:0] = out_31; _31[31:0] = out_35; _32[31:0] = out_39; left = x_left; reg_x[30:0] = out_5;
  //   reg_y[31:0] = out_6; right = x_right; start_alt_1 = start;
  //   x_inverted[30:0] = {x_final[0], x_final[1], x_final[2], x_final[3], x_final[4], x_final[5], x_final[6], x_final[7], x_final[8], x_final[9], x_final[10], x_final[11], x_final[12], x_final[13], x_final[14], x_final[15], x_final[16], x_final[17], x_final[18], x_final[19], x_final[20], x_final[21], x_final[22], x_final[23], x_final[24], x_final[25], x_final[26], x_final[27], x_final[28], x_final[29], x_final[30]};
  //   x_medium[30:0] = {x_inverted_alt[0], x_inverted_alt[1], x_inverted_alt[2], x_inverted_alt[3], x_inverted_alt[4], x_inverted_alt[5], x_inverted_alt[6], x_inverted_alt[7], x_inverted_alt[8], x_inverted_alt[9], x_inverted_alt[10], x_inverted_alt[11], x_inverted_alt[12], x_inverted_alt[13], x_inverted_alt[14], x_inverted_alt[15], x_inverted_alt[16], x_inverted_alt[17], x_inverted_alt[18], x_inverted_alt[19], x_inverted_alt[20], x_inverted_alt[21], x_inverted_alt[22], x_inverted_alt[23], x_inverted_alt[24], x_inverted_alt[25], x_inverted_alt[26], x_inverted_alt[27], x_inverted_alt[28], x_inverted_alt[29], x_inverted_alt[30]}

  // Notes on the sheet:
  //   Bottom line
  //   Field options
  //   Top line
  //   Сollision avoidance
  //   Player Position
  //   Checking for a hole
  //   Losing indicator
endmodule

module check_helper (
  input  [31:0] in_1,
  input  [31:0] in_2,
  output out_3
);

  wire or_1_out;
  wire [31:0] and_1_out;

  assign and_1_out = in_1 & in_2;  // AND_Gate and_1, 32 bits wide
  or or_1 (or_1_out, and_1_out[0], and_1_out[1], and_1_out[2], and_1_out[3], and_1_out[4], and_1_out[5], and_1_out[6], and_1_out[7], and_1_out[8], and_1_out[9], and_1_out[10], and_1_out[11], and_1_out[12], and_1_out[13], and_1_out[14], and_1_out[15], and_1_out[17], and_1_out[18], and_1_out[19], and_1_out[20], and_1_out[21], and_1_out[22], and_1_out[23], and_1_out[24], and_1_out[25], and_1_out[26], and_1_out[27], and_1_out[28], and_1_out[29], and_1_out[30], and_1_out[31], and_1_out[16]);
  not not_1 (out_3, or_1_out);
endmodule

module Info_Screen (
  input  Lose_indicator,
  input  Start,
  input  Pause,
  output [31:0] out_4,
  output [31:0] out_5,
  output [31:0] out_6,
  output [31:0] out_7,
  output [31:0] out_8,
  output [31:0] out_9,
  output [31:0] out_10
);

  wire not_1_out;
  wire [1:0] indicator;

  D_Flip_Flop d_ff_1 (.clk(Pause), .D(not_1_out), .Q(indicator[1]));  // open: Qn, preset, en, reset
  not not_1 (not_1_out, indicator[1]);
  D_Flip_Flop d_ff_2 (
    .clk(Lose_indicator), .D(Lose_indicator), .Q(indicator[0]), .reset(Start));  // open: Qn, preset, en
  Multiplexer #(.select(2), .width(32), .enable("false")) multiplexer_1 (
    .in0({32{1'b0}}), .in1(32'he7bde23e), .in2(32'hf3c91cf0), .in3(32'he7bde23e), .out(out_4), .sel(indicator));
  Multiplexer #(.select(2), .width(32), .enable("false")) multiplexer_2 (
    .in0({32{1'b0}}), .in1(32'h94210508), .in2(32'h92492080), .in3(32'h94210508), .out(out_5), .sel(indicator));
  Multiplexer #(.select(2), .width(32), .enable("false")) multiplexer_3 (
    .in0({32{1'b0}}), .in1(32'h94210888), .in2(32'h92492080), .in3(32'h94210888), .out(out_6), .sel(indicator));
  Multiplexer #(.select(2), .width(32), .enable("false")) multiplexer_4 (
    .in0({32{1'b0}}), .in1(32'h97bdef88), .in2(32'hf3c918e0), .in3(32'h97bdef88), .out(out_7), .sel(indicator));
  Multiplexer #(.select(2), .width(32), .enable("false")) multiplexer_5 (
    .in0({32{1'b0}}), .in1(32'h94210888), .in2(32'h82490480), .in3(32'h94210888), .out(out_8), .sel(indicator));
  Multiplexer #(.select(2), .width(32), .enable("false")) multiplexer_6 (
    .in0({32{1'b0}}), .in1(32'h94210888), .in2(32'h82490480), .in3(32'h94210888), .out(out_9), .sel(indicator));
  Multiplexer #(.select(2), .width(32), .enable("false")) multiplexer_7 (
    .in0({32{1'b0}}), .in1(32'he7a1e888), .in2(32'h824638f0), .in3(32'he7a1e888), .out(out_10),
    .sel(indicator));

  // Other names for the same wires on the sheet: lose = indicator[0]; pause_t = indicator[1]
endmodule

module keyboard (
  input  [6:0] keyboard,
  output right,
  output left,
  output start
);

  Comparator #(.width(7)) comparator_1 (.a(keyboard), .b(7'b1100100), .eq(right));  // open: gt, lt
  Comparator #(.width(7)) comparator_2 (.a(keyboard), .b(7'b1100001), .eq(left));  // open: gt, lt
  Comparator #(.width(7)) comparator_3 (.a(keyboard), .b(7'b0001010), .eq(start));  // open: gt, lt
endmodule
